# Fritzing sketch Sequencer Sketch rev1-0 (saved by Fritzing 0.9.9b)
breadboards: 1

parts:
  Raspberry_Pi_1 = Raspberry Pi 3 [part_number=RPI-3-V1.2]
  R1 = Resistor [tolerance=±5% power=0.25 resistance=330 package=THT]
  R2 = Resistor [tolerance=±5% power=0.25 resistance=330 package=THT]
  R3 = Resistor [tolerance=±5% power=0.25 resistance=330 package=THT]
  R4 = Resistor [tolerance=±5% power=0.25 resistance=330 package=THT]
  R5 = Resistor [tolerance=±5% power=0.25 resistance=330 package=THT]
  R6 = Resistor [tolerance=±5% power=0.25 resistance=330 package=THT]
  R7 = Resistor [tolerance=±5% power=0.25 resistance=330 package=THT]
  R8 = Resistor [tolerance=±5% power=0.25 resistance=330 package=THT]
  LED1 = LED - 5mm [color="Red (633nm)" current=0.030 package="5 mm [THT]"]
  LED2 = LED - 5mm [color="Red (633nm)" current=0.030 package="5 mm [THT]"]
  LED3 = LED - 5mm [color="Red (633nm)" current=0.030 package="5 mm [THT]"]
  LED4 = LED - 5mm [color="Red (633nm)" current=0.030 package="5 mm [THT]"]
  LED5 = LED - 5mm [color="Red (633nm)" current=0.030 package="5 mm [THT]"]
  LED6 = LED - 5mm [color="Red (633nm)" current=0.030 package="5 mm [THT]"]
  LED7 = LED - 5mm [color="Red (633nm)" current=0.030 package="5 mm [THT]"]
  LED8 = LED - 5mm [color="Red (633nm)" current=0.030 package="5 mm [THT]"]
  LCD1 = LCD screen
  IC1 = IC, DIP package, 10 pins [chip_label="I²C to LCD"]
  RE1 = Rotary Encoder [package=THT]
  RE2 = Rotary Encoder [package=THT]
  RE3 = Rotary Encoder [package=THT]
  RE4 = Rotary Encoder [package=THT]
  RE5 = Rotary Encoder [package=THT]
  RE6 = Rotary Encoder [package=THT]
  RE7 = Rotary Encoder [package=THT]
  RE8 = Rotary Encoder [package=THT]
  S1 = Pushbutton [package=THT]
  TRS1 = Audio Jack (TRS) 3.5mm [package="4Ucon 08780 [THT]"]
  TRS2 = Audio Jack (TRS) 3.5mm [package="4Ucon 08780 [THT]"]
  TRS3 = Audio Jack (TRS) 3.5mm [package="4Ucon 08780 [THT]"]
  TRS4 = Audio Jack (TRS) 3.5mm [package="4Ucon 08780 [THT]"]
  TRS5 = Audio Jack (TRS) 3.5mm [package="4Ucon 08780 [THT]"]
  IC2 = IC, DIP package, 6 pins [chip_label="DAC 1"]
  IC3 = IC, DIP package, 20 pins [chip_label="DAC 2"]
  U1 = PCF8574 [package="DIP16 [THT]"]

nets:
  3V3: Raspberry_Pi_1.3v3, LCD1.LED+, IC1.pin1, U1.VCC
  N1: Raspberry_Pi_1.GPIO2, IC1.pin2, U1.SDA
  N2: Raspberry_Pi_1.GPIO3, IC1.pin3, U1.SCL
  N3: Raspberry_Pi_1.GPIO4, RE8.EncoderPinB
  N4: Raspberry_Pi_1.GPIO17, RE6.EncoderPinB
  N5: Raspberry_Pi_1.GPIO27, RE6.EncoderPinA
  N6: Raspberry_Pi_1.GPIO22, RE5.EncoderPinA
  N7: Raspberry_Pi_1.GPIO10, IC2.pin2, IC3.pin2
  N8: Raspberry_Pi_1.GPIO9, RE3.EncoderPinB
  N9: Raspberry_Pi_1.GPIO11, IC2.pin6, IC3.pin20
  GND: Raspberry_Pi_1.GND, R1.Pin_0, R2.Pin_0, R3.Pin_0, R4.Pin_0, R5.Pin_0, R6.Pin_0, R7.Pin_0, R8.Pin_0, LCD1.VSS, LCD1.LED-, IC1.pin6, RE1.EncoderPinC, RE2.EncoderPinC, RE3.EncoderPinC, RE4.EncoderPinC, RE5.EncoderPinC, RE6.EncoderPinC, RE7.EncoderPinC, RE8.EncoderPinC, S1.leg0, TRS1.Sleeve, TRS2.Sleeve, TRS3.Sleeve, TRS4.Sleeve, TRS5.Sleeve, IC2.pin4, IC3.pin11, IC3.pin14, U1.GND
  N10: Raspberry_Pi_1.ID_SD, RE3.EncoderPinA
  N11: Raspberry_Pi_1.GPIO5, RE2.EncoderPinB
  N12: Raspberry_Pi_1.GPIO6, RE1.EncoderPinB
  N13: Raspberry_Pi_1.GPIO13, RE1.EncoderPinA
  N14: Raspberry_Pi_1.GPIO19, S1.leg1
  N15: Raspberry_Pi_1.GPIO16, IC3.pin13
  N16: Raspberry_Pi_1.GPIO12, RE2.EncoderPinA
  N17: Raspberry_Pi_1.ID_SC, IC3.pin15
  N18: Raspberry_Pi_1.GPIO7, IC3.pin16
  N19: Raspberry_Pi_1.GPIO8, IC2.pin5
  N20: Raspberry_Pi_1.GPIO25, RE4.EncoderPinA
  N21: Raspberry_Pi_1.GPIO24, RE4.EncoderPinB
  N22: Raspberry_Pi_1.GPIO23, RE5.EncoderPinB
  N23: Raspberry_Pi_1.GPIO18, RE7.EncoderPinA
  N24: Raspberry_Pi_1.GPIO15, RE7.EncoderPinB
  N25: Raspberry_Pi_1.GPIO14, RE8.EncoderPinA
  5V: Raspberry_Pi_1.5V, LCD1.VDD, IC2.pin1, IC3.pin1
  N26: LED1.anode, U1.P0
  N27: LED2.anode, U1.P1
  N28: LED3.anode, U1.P2
  N29: LED4.anode, U1.P3
  N30: LED5.anode, U1.P4
  N31: LED6.anode, U1.P5
  N32: LED7.anode, U1.P6
  N33: LED8.anode, U1.P7
  N34: LCD1.V0, IC1.pin7
  N35: LCD1.RS, IC1.pin8
  N36: LCD1.R/W, IC1.pin9
  N37: LCD1.E, IC1.pin10
  N38: TRS1.Tip, IC3.pin9
  N39: TRS2.Tip, IC3.pin8
  N40: TRS3.Tip, IC3.pin7
  N41: TRS4.Tip, IC3.pin6
  N42: TRS5.Tip, IC2.pin3
